// Logisim project FULL SUBTRACTOR.circ as structural Verilog: 1 circuit, main circuit main
module main (
  input  AB,
  input  B,
  input  C,
  output out_4,
  output out_5
);

  wire and_1_out, and_2_out, and_3_out, not_1_out;

  not not_1 (not_1_out, AB);
  ExactlyOne xor_1 (.out(out_4), .in0(AB), .in1(B), .in2(C));
  and and_1 (and_1_out, not_1_out, B);
  and and_2 (and_2_out, B, C);
  and and_3 (and_3_out, not_1_out, C);
  or or_1 (out_5, and_1_out, and_2_out, and_3_out);

  // Notes on the sheet:
  //   DIFFERENCE
  //   BORROW
endmodule
