// Logisim project HALF SUBTRACTOR.circ as structural Verilog: 1 circuit, main circuit main
module main (
  input  A,
  input  B,
  input  A_2,
  input  B_2,
  output out_5,
  output out_6,
  output out_7,
  output out_8
);

  wire not_1_out, not_2_out;

  not not_1 (not_1_out, A);
  not not_2 (not_2_out, A_2);
  xor xor_1 (out_5, A, B);
  and and_1 (out_6, not_1_out, B);
  xor xor_2 (out_7, A_2, B_2);
  and and_2 (out_8, not_2_out, B_2);

  // Notes on the sheet:
  //   HALF SUBTRACTER
  //   HALF SUBTRACTER
  //   BORROW
  //   DIFFERENCE
  //   DIFFERENCE
  //   BORROW
endmodule
