// Logisim project full adder.circ as structural Verilog: 1 circuit, main circuit main
module main (
  input  in_1,
  input  B,
  input  C,
  output SUM,
  output CARRY
);

  wire and_1_out, and_2_out, and_3_out;

  ExactlyOne xor_1 (.out(SUM), .in0(in_1), .in1(B), .in2(C));
  and and_1 (and_1_out, in_1, B);
  and and_2 (and_2_out, B, C);
  and and_3 (and_3_out, C, in_1);
  or or_1 (CARRY, and_2_out, and_3_out);

  // Notes on the sheet:
  //   A
  //   A.B
  //   B.C
  //   C.A
  //   FULL ADDER
endmodule
