// Logisim project half adder.circ as structural Verilog: 1 circuit, main circuit main
module main (
  input  in_1,
  input  in_2,
  input  B,
  input  B_2,
  input  in_5,
  input  in_6,
  input  B_3,
  input  B_4,
  output out_9,
  output out_10,
  output out_11,
  output out_12,
  output out_13,
  output out_14,
  output out_15,
  output out_16
);

  xor xor_1 (out_10, in_2, B_2);
  and and_1 (out_12, in_2, B_2);
  xor xor_2 (out_13, in_5, B_3);
  and and_2 (out_15, in_5, B_3);
  xor xor_3 (out_9, in_1, B);
  and and_3 (out_11, in_1, B);
  xor xor_4 (out_14, in_6, B_4);
  and and_4 (out_16, in_6, B_4);

  // Notes on the sheet:
  //   A
  //   A
  //   HALF ADDER
  //   SUm
  //   CARRY
  //   SUm
  //   CARRY
  //   A
  //   A
  //   SUm
  //   CARRY
  //   SUm
  //   CARRY
endmodule
